// Digital circuit ALU.dig as structural Verilog
module ALU (
  input  [7:0] CMD,
  input  [7:0] DAT,
  input  CLK,
  output [7:0] Q
);

  wire _8_input_or_1_p2, _8_input_or_2_p2, adder_subtractor_1_c_8, adder_subtractor_1_f,
       adder_subtractor_1_stc, adder_subtractor_1_stf, comparator_1_eq, comparator_2_eq, comparator_3_eq,
       comparator_4_eq, comparator_5_eq, comparator_6_eq, comparator_7_eq, comparator_8_eq, comparator_9_eq,
       comparator_10_eq, comparator_11_eq, comparator_12_eq, comparator_13_eq, comparator_14_eq,
       comparator_15_eq, comparator_16_eq, comparator_17_eq, comparator_18_eq, comparator_19_eq,
       comparator_20_eq, comparator_22_eq, comparator_23_eq, comparator_24_eq, comparator_25_eq,
       comparator_26_eq, comparator_27_eq, comparator_28_eq, comparator_29_eq, flag_register_1_c,
       incrementor_1_q_s, or_1_out;
  wire [7:0] register_1_val, register_2_val;

  Comparator #(.Bits(8)) comparator_1 (.a(CMD), .b(8'h20), .eq(comparator_1_eq));  // open: gt, lt
  Comparator #(.Bits(8)) comparator_2 (.a(CMD), .b(8'h21), .eq(comparator_2_eq));  // open: gt, lt
  Comparator #(.Bits(8)) comparator_3 (.a(CMD), .b(8'h22), .eq(comparator_3_eq));  // open: gt, lt
  Comparator #(.Bits(8)) comparator_4 (.a(CMD), .b(8'h23), .eq(comparator_4_eq));  // open: gt, lt
  Comparator #(.Bits(8)) comparator_5 (.a(CMD), .b(8'h13), .eq(comparator_5_eq));  // open: gt, lt
  Comparator #(.Bits(8)) comparator_6 (.a(CMD), .b(8'h14), .eq(comparator_6_eq));  // open: gt, lt
  or or_1 (or_1_out, comparator_5_eq, incrementor_1_q_s);
  Register register_1 (.D(DAT), .STR(comparator_1_eq), .LD(comparator_2_eq), .CLK(CLK), .VAL(register_1_val), .Q(Q));
  Register register_2 (.D(DAT), .STR(comparator_3_eq), .LD(comparator_4_eq), .CLK(CLK), .VAL(register_2_val), .Q(Q));
  Register register_3 (.D(DAT), .STR(or_1_out), .LD(comparator_6_eq), .CLK(CLK), .VAL(register_2_val), .Q(Q));
  Comparator #(.Bits(8)) comparator_7 (.a(CMD), .b(8'h24), .eq(comparator_7_eq));  // open: gt, lt
  Comparator #(.Bits(8)) comparator_8 (.a(CMD), .b(8'h25), .eq(comparator_8_eq));  // open: gt, lt
  Comparator #(.Bits(8)) comparator_9 (.a(CMD), .b(8'h26), .eq(comparator_9_eq));  // open: gt, lt
  Comparator #(.Bits(8)) comparator_10 (.a(CMD), .b(8'h27), .eq(comparator_10_eq));  // open: gt, lt
  Comparator #(.Bits(8)) comparator_11 (.a(CMD), .b(8'he), .eq(comparator_11_eq));  // open: gt, lt
  Comparator #(.Bits(8)) comparator_12 (.a(CMD), .b(8'hf), .eq(comparator_12_eq));  // open: gt, lt
  Comparator #(.Bits(8)) comparator_13 (.a(CMD), .b(8'h10), .eq(comparator_13_eq));  // open: gt, lt
  Comparator #(.Bits(8)) comparator_14 (.a(CMD), .b(8'h11), .eq(comparator_14_eq));  // open: gt, lt
  Comparator #(.Bits(8)) comparator_15 (.a(CMD), .b(8'h12), .eq(comparator_15_eq));  // open: gt, lt
  Comparator #(.Bits(8)) comparator_16 (.a(CMD), .b(8'h1d), .eq(comparator_16_eq));  // open: gt, lt
  Comparator #(.Bits(8)) comparator_17 (.a(CMD), .b(8'h1e), .eq(comparator_17_eq));  // open: gt, lt
  Comparator #(.Bits(8)) comparator_18 (.a(CMD), .b(8'h1f), .eq(comparator_18_eq));  // open: gt, lt
  Comparator #(.Bits(8)) comparator_19 (.a(CMD), .b(8'h28), .eq(comparator_19_eq));  // open: gt, lt
  Comparator #(.Bits(8)) comparator_20 (.a(CMD), .b(8'h29), .eq(comparator_20_eq));  // open: gt, lt
  Flag_Register flag_register_1 (
    .DAT(DAT), .C_8(adder_subtractor_1_c_8), .F(adder_subtractor_1_f), .STC(adder_subtractor_1_stc),
    .STF(adder_subtractor_1_stf), .STA(comparator_7_eq), .LDC(comparator_8_eq), .LDF(comparator_9_eq),
    .LDA(comparator_10_eq), .CLK(CLK), .Q(Q), .C(flag_register_1_c));
  Adder_Subtractor adder_subtractor_1 (
    .C_in(flag_register_1_c), .A(register_1_val), .B(register_2_val), .ADD(comparator_11_eq),
    .ADC(comparator_12_eq), .SUB(comparator_13_eq), .CLK(CLK), .Q(Q), .C_8(adder_subtractor_1_c_8),
    .F(adder_subtractor_1_f), .STC(adder_subtractor_1_stc), .STF(adder_subtractor_1_stf));
  Incrementor incrementor_1 (
    .C(register_2_val), .INC(comparator_14_eq), .DEC(comparator_15_eq), .CLK(CLK), .Q(Q),
    .C_8(adder_subtractor_1_c_8), .F(adder_subtractor_1_f), .STC(adder_subtractor_1_stc),
    .STF(adder_subtractor_1_stf), .Q_S(incrementor_1_q_s));
  Comparator comparator_21 (
    .A(register_1_val), .B(register_2_val), .CMP_bigger(comparator_16_eq), .CMP_equal(comparator_17_eq),
    .CMP_smaller(comparator_18_eq), .CLK(CLK), .Q(Q));
  Barrel_Shift_Register barrel_shift_register_1 (
    .A(register_1_val), .DIS(DAT), .SFT(comparator_19_eq), .SFC(comparator_20_eq), .CLK(CLK), .Q(Q));
  Comparator #(.Bits(8)) comparator_22 (.a(CMD), .b(8'h15), .eq(comparator_22_eq));  // open: gt, lt
  Comparator #(.Bits(8)) comparator_23 (.a(CMD), .b(8'h16), .eq(comparator_23_eq));  // open: gt, lt
  Comparator #(.Bits(8)) comparator_24 (.a(CMD), .b(8'h17), .eq(comparator_24_eq));  // open: gt, lt
  Comparator #(.Bits(8)) comparator_25 (.a(CMD), .b(8'h18), .eq(comparator_25_eq));  // open: gt, lt
  Comparator #(.Bits(8)) comparator_26 (.a(CMD), .b(8'h19), .eq(comparator_26_eq));  // open: gt, lt
  Comparator #(.Bits(8)) comparator_27 (.a(CMD), .b(8'h1a), .eq(comparator_27_eq));  // open: gt, lt
  Comparator #(.Bits(8)) comparator_28 (.a(CMD), .b(8'h1b), .eq(comparator_28_eq));  // open: gt, lt
  Comparator #(.Bits(8)) comparator_29 (.a(CMD), .b(8'h1c), .eq(comparator_29_eq));  // open: gt, lt
  // _8_Input_Or _8_input_or_1: pin names not known; wires that end beside it: register_1_val, _8_input_or_1_p2
  // _8_Input_Or _8_input_or_2: pin names not known; wires that end beside it: register_2_val, _8_input_or_2_p2
  Binary_NOT binary_not_1 (.A(_8_input_or_1_p2), .EN(comparator_22_eq), .CLK(CLK), .Q(Q));
  Binary_OR binary_or_1 (.A(_8_input_or_1_p2), .B(_8_input_or_2_p2), .EN(comparator_23_eq), .CLK(CLK), .Q(Q));
  Binary_AND binary_and_1 (.A(_8_input_or_1_p2), .B(_8_input_or_2_p2), .EN(comparator_24_eq), .CLK(CLK), .Q(Q));
  Binary_XOR binary_xor_1 (.A(_8_input_or_1_p2), .B(_8_input_or_2_p2), .EN(comparator_25_eq), .CLK(CLK), .Q(Q));
  Bitwise_NOT bitwise_not_1 (.A(register_1_val), .EN(comparator_26_eq), .CLK(CLK), .Q(Q));
  Bitwise_OR bitwise_or_1 (.A(register_1_val), .B(register_2_val), .EN(comparator_27_eq), .CLK(CLK));  // open: Q
  Bitwise_AND bitwise_and_1 (.A(register_1_val), .B(register_2_val), .EN(comparator_28_eq), .CLK(CLK), .Q(Q));
  Bitwise_XOR bitwise_xor_1 (.A(register_1_val), .B(register_2_val), .EN(comparator_29_eq), .CLK(CLK), .Q(Q));

  // Notes on the sheet:
  //   CMD
  //   DAT
  //   CLK
  //   A
  //   B
  //   C
  //   Q
endmodule
