// Digital circuit CPU.dig as structural Verilog
module CPU (
  input  clk,
  input  CLR_PC,
  input  STR
);

  wire comparator_1_eq, comparator_2_eq, comparator_3_eq, comparator_4_eq, comparator_5_eq, comparator_6_eq,
       comparator_7_eq, comparator_8_eq, comparator_9_eq, comparator_10_eq, comparator_11_eq,
       flash_memory_1_p3, programme_counter_1_p2, programme_counter_1_p7;
  wire [3:0] register_1_p5, register_1_p5_2;
  wire [7:0] dipswitch_1_out, flash_memory_1_p2, flash_memory_1_p5, programme_counter_1_p1;

  LED led_1 (.in(dipswitch_1_out[0]));
  LED led_2 (.in(dipswitch_1_out[1]));
  DipSwitch dipswitch_1 (.out(dipswitch_1_out[0]));
  DipSwitch dipswitch_2 (.out(dipswitch_1_out[1]));
  LED led_3 (.in(dipswitch_1_out[2]));
  LED led_4 (.in(dipswitch_1_out[3]));
  DipSwitch dipswitch_3 (.out(dipswitch_1_out[2]));
  DipSwitch dipswitch_4 (.out(dipswitch_1_out[3]));
  LED led_5 (.in(dipswitch_1_out[4]));
  LED led_6 (.in(dipswitch_1_out[5]));
  DipSwitch dipswitch_5 (.out(dipswitch_1_out[4]));
  DipSwitch dipswitch_6 (.out(dipswitch_1_out[5]));
  LED led_7 (.in(dipswitch_1_out[6]));
  LED led_8 (.in(dipswitch_1_out[7]));
  DipSwitch dipswitch_7 (.out(dipswitch_1_out[6]));
  DipSwitch dipswitch_8 (.out(dipswitch_1_out[7]));
  Comparator #(.Bits(8)) comparator_1 (.a(flash_memory_1_p5), .b(8'h1), .eq(comparator_1_eq));  // open: gt, lt
  Comparator #(.Bits(8)) comparator_2 (.a(flash_memory_1_p5), .b(8'h2), .eq(comparator_2_eq));  // open: gt, lt
  Comparator #(.Bits(8)) comparator_3 (.a(flash_memory_1_p5), .b(8'h3), .eq(comparator_3_eq));  // open: gt, lt
  Comparator #(.Bits(8)) comparator_4 (.a(flash_memory_1_p5), .b(8'h4), .eq(comparator_4_eq));  // open: gt, lt
  Comparator #(.Bits(8)) comparator_5 (.a(flash_memory_1_p5), .b(8'h5), .eq(comparator_5_eq));  // open: gt, lt
  Comparator #(.Bits(8)) comparator_6 (.a(flash_memory_1_p5), .b(8'h6), .eq(comparator_6_eq));  // open: gt, lt
  Comparator #(.Bits(8)) comparator_7 (.a(flash_memory_1_p5), .b(8'h7), .eq(comparator_7_eq));  // open: gt, lt
  Comparator #(.Bits(8)) comparator_8 (.a(flash_memory_1_p5), .b(8'h24), .eq(comparator_8_eq));  // open: gt, lt
  Comparator #(.Bits(8)) comparator_9 (.a(flash_memory_1_p5), .b(8'h24), .eq(comparator_9_eq));  // open: gt, lt
  Comparator #(.Bits(8)) comparator_10 (.a(flash_memory_1_p5), .b(8'h25), .eq(comparator_10_eq));  // open: gt, lt
  Comparator #(.Bits(8)) comparator_11 (.a(flash_memory_1_p5), .b(8'h26), .eq(comparator_11_eq));  // open: gt, lt
  // Programme_Counter programme_counter_1: pin names not known; wires that end beside it: programme_counter_1_p1, programme_counter_1_p2, clk, comparator_1_eq, comparator_2_eq, CLR_PC, programme_counter_1_p7
  // Flash_Memory flash_memory_1: pin names not known; wires that end beside it: programme_counter_1_p7, flash_memory_1_p2, flash_memory_1_p3, clk, flash_memory_1_p5, programme_counter_1_p1, programme_counter_1_p2, programme_counter_1_p1
  ALU alu_1 (.CMD(flash_memory_1_p5), .DAT(programme_counter_1_p1), .CLK(clk), .Q(flash_memory_1_p2));
  // DAT_to_ADR_interface dat_to_adr_interface_1: pin names not known; wires that end beside it: programme_counter_1_p1, comparator_3_eq, comparator_4_eq, comparator_5_eq, clk, programme_counter_1_p2, flash_memory_1_p3
  // RAM ram_1: pin names not known; wires that end beside it: programme_counter_1_p1, programme_counter_1_p2, comparator_6_eq, comparator_7_eq, clk, programme_counter_1_p1
  // Register register_1: pin names not known; wires that end beside it: dipswitch_1_out, STR, comparator_8_eq, clk, {register_1_p5_2, register_1_p5}, programme_counter_1_p1
  // Input_Control input_control_1: pin names not known; wires that end beside it: STR, comparator_9_eq, clk, programme_counter_1_p1
  // Register register_2: pin names not known; wires that end beside it: programme_counter_1_p1, comparator_10_eq, comparator_11_eq, clk, programme_counter_1_p1, flash_memory_1_p5, programme_counter_1_p1, programme_counter_1_p2
  Seven_Seg_Hex seven_seg_hex_1 (.d(register_1_p5), .dp(1'b0));
  Seven_Seg_Hex seven_seg_hex_2 (.d(register_1_p5_2), .dp(1'b0));
  LED led_9 (.in(register_1_p5[0]));
  LED led_10 (.in(register_1_p5[1]));
  LED led_11 (.in(register_1_p5[2]));
  LED led_12 (.in(register_1_p5[3]));
  LED led_13 (.in(register_1_p5_2[0]));
  LED led_14 (.in(register_1_p5_2[1]));
  LED led_15 (.in(register_1_p5_2[2]));
  LED led_16 (.in(register_1_p5_2[3]));

  // Notes on the sheet:
  //   clk: Hz: 5
  //   CMD
  //   DAT
  //   ADR
  //   CLK
  //   LN: current line of code being executed
  //   commands requiring the address bus to be disabled:
  //   Bus Transfer:
  //   - load from interface registers
  //   commands requiring the data bus to be disabled:
  //   Storage: 
  //   - load > data
  //   ALU:
  //   - add > data
  //   - add with carry > data
  //   - subtract > data
  //   incrementor:
  //   - increment > data
  //   - decrement > data
  //   logic:
  //   - binary not
  //   - binary or
  //   - binary and
  //   - binary xor
  //   - bitwise not
  //   - bitwise or
  //   - bitwise and
  //   - bitwise xor
  //   a/b/c registers:
  //   - load a > data
  //   - load b > data
  //   - load c > data
  //   compare:
  //   - bigger > data
  //   - equal > data
  //   - smaller > data
  //   flag reg:
  //   - load carry > data
  //   - load overflow > data
  //   - load flags > data
endmodule
